# Fritzing sketch schema (saved by Fritzing 0.9.6b)
breadboards: 1

parts:
  Mod1 = Heltec WiFi LoRa 32 V2 [part_number=HTIT-WB32LA]
  Mod2 = KY-023 Dual Axis Joystick Module [package="Breakout board"]
  S1 = Pushbutton [package="[THT]"]
  S2 = Pushbutton [package="[THT]"]
  R1 = Resistor [tolerance=±5% resistance=10k package="0805 [SMD]"]
  R2 = Resistor [tolerance=±5% resistance=10k package="0805 [SMD]"]
  LED1 = smd LED [color="Red (633nm)" package="0603 [SMD]"]  # not connected
  LED2 = smd LED [color="Yellow (595nm)" package="0603 [SMD]"]
  R3 = Resistor [tolerance=±5% resistance=220 package="0805 [SMD]"]
  R4 = Resistor [tolerance=±5% resistance=220 package="0805 [SMD]"]

nets:
  N1: Mod1.pin_6, LED2.anode
  N2: Mod1.pin_7, S1.Pin_3, S1.Pin_4, R1.Pin_0
  N3: Mod1.pin_8, S2.Pin_3, S2.Pin_4, R2.Pin_0
  N4: Mod1.pin_9, Mod2.VRy
  N5: Mod1.pin_10, Mod2.VRx
  N6: Mod1.pin_16, Mod1.pin_17, Mod2.+5V, S1.Pin_1, S1.Pin_2, S2.Pin_1, S2.Pin_2
  GND: Mod1.GND, Mod2.GND, R1.Pin_1, R2.Pin_1, R3.Pin_1, R4.Pin_1
  N7: LED2.cathode, R3.Pin_0

custom parts:
  KY-023 Dual Axis Joystick Module: KY-023 Dual-Axis Joystick Module.
